// Logisim project schema.circ as structural Verilog: 1 circuit, main circuit main
module main (
  input  in_1,
  input  in_2,
  input  in_3,
  input  in_4
);

  wire Alu2_GT_Alu1, Alu_1_In, Alu_2_In, Alu_Op_H, Alu_Op_L, Alu_Out, and_1_out, and_2_out, and_3_out,
       and_4_out, and_5_out, and_6_out, and_7_out, and_8_out, and_9_out, and_10_out, and_11_out, and_12_out,
       and_13_out, button_2_out, Carry_In, Carry_out, clock, clock_1_out, decoder_1_out0, decoder_1_out1,
       decoder_1_out2, decoder_1_out3, decoder_2_out0, decoder_2_out1, decoder_2_out2, decoder_2_out3,
       demultiplexer_1_out0, demultiplexer_1_out1, demultiplexer_2_out0, demultiplexer_2_out1,
       demultiplexer_3_out0, demultiplexer_3_out1, demultiplexer_4_out0, demultiplexer_4_out1,
       demultiplexer_5_out0, demultiplexer_5_out1, FF_Out, Flag_negative, Flag_zero, Halt,
       Instruction_Register_Enable, IP_Advance, IP_Enable, IP_Out, IP_Select, JMP_Enable, JMP_In, JMP_Select,
       Memory_In, Memory_Input_Select, Memory_out, Micro_Reset, nor_1_out, not_1_out, One_Out, or_1_out,
       Register_In_Enable, Register_In_H, Register_In_L, Register_Out_Enable, Register_Out_H, Register_Out_L,
       Reset, Reset_Button, RET_Enable, RET_In, RET_Select, SP_Enable, SP_In, SP_Select, Write_Memory_Enable,
       Write_Memory_Select;
  wire [3:0] Micro_Counter;
  wire [7:0] adder_1_out, Bus, Instruction, Jump_Register_High, Jump_Register_Low, Memory_Register_High,
       Memory_Register_Low, multiplexer_4_out, nand_1_out, Register_A, Register_ALU_1, Register_ALU_2,
       Register_B, Register_C, Register_D, RET_Register_High, RET_Register_Low, Stack_Pointer_High,
       Stack_Pointer_Low, subtractor_1_out, xor_1_out;
  wire [15:0] Instruction_Pointer, multiplexer_1_out, multiplexer_2_out;
  wire [23:0] rom_1_data;
  wire [31:6] rom_2_data;

  Demultiplexer #(.disabled(0)) demultiplexer_1 (
    .out0(demultiplexer_1_out0), .out1(demultiplexer_1_out1), .in(IP_Enable), .sel(IP_Select), .en(IP_Out));
  Demultiplexer #(.enable("false")) demultiplexer_2 (
    .out0(demultiplexer_2_out0), .out1(demultiplexer_2_out1), .in(Write_Memory_Enable),
    .sel(Write_Memory_Select));
  Register High (.D(Bus), .en(demultiplexer_2_out1), .Q(Memory_Register_High), .clk(clock), .clr(Reset));
  Multiplexer #(.width(16), .enable("false")) multiplexer_1 (
    .in0(Instruction_Pointer), .in1({Memory_Register_High, Memory_Register_Low}), .out(multiplexer_1_out),
    .sel(Memory_Input_Select));
  and and_1 (and_1_out, ~SP_Select, SP_Enable, SP_In);  // AND_Gate
  and and_2 (and_2_out, ~SP_In, SP_Enable);  // AND_Gate
  Demultiplexer #(.enable("false")) demultiplexer_3 (
    .out0(demultiplexer_3_out0), .out1(demultiplexer_3_out1), .in(and_2_out), .sel(SP_Select));
  and and_3 (and_3_out, ~JMP_In, JMP_Enable);  // AND_Gate
  and and_4 (and_4_out, ~JMP_Select, JMP_Enable, JMP_In);  // AND_Gate
  Demultiplexer #(.enable("false")) demultiplexer_4 (
    .out0(demultiplexer_4_out0), .out1(demultiplexer_4_out1), .in(and_3_out), .sel(JMP_Select));
  and and_5 (and_5_out, ~RET_Select, RET_Enable, RET_In);  // AND_Gate
  and and_6 (and_6_out, ~RET_In, RET_Enable);  // AND_Gate
  Demultiplexer #(.enable("false")) demultiplexer_5 (
    .out0(demultiplexer_5_out0), .out1(demultiplexer_5_out1), .in(and_6_out), .sel(RET_Select));
  Multiplexer #(.width(8), .enable("false")) multiplexer_2 (
    .in0(Instruction_Pointer[7:0]), .in1(Bus), .out(multiplexer_2_out[7:0]), .sel(and_7_out));
  and and_7 (and_7_out, ~IP_Select, ~IP_Out, IP_Enable);  // AND_Gate
  Multiplexer #(.width(8), .enable("false")) multiplexer_3 (
    .in0(Instruction_Pointer[15:8]), .in1(Bus), .out(multiplexer_2_out[15:8]), .sel(and_8_out));
  and and_8 (and_8_out, IP_Select, ~IP_Out, IP_Enable);  // AND_Gate
  or or_1 (or_1_out, and_7_out, and_8_out);
  Register Low (.D(Bus), .en(demultiplexer_2_out0), .Q(Memory_Register_Low), .clk(clock), .clr(Reset));
  Register register_1 (.D(Bus), .en(Instruction_Register_Enable), .Q(Instruction), .clk(clock), .clr(Reset));
  and and_9 (and_9_out, SP_Select, SP_Enable, SP_In);
  and and_10 (and_10_out, JMP_Select, JMP_Enable, JMP_In);
  and and_11 (and_11_out, RET_Select, RET_Enable, RET_In);
  assign Bus = One_Out ? 8'h1 : 8'bz;  // Controlled_Buffer controlled_buffer_1
  assign Bus = FF_Out ? {8{1'b1}} : 8'bz;  // Controlled_Buffer controlled_buffer_2
  assign Bus = demultiplexer_1_out0 ? Instruction_Pointer[7:0] : 8'bz;  // Controlled_Buffer controlled_buffer_3
  assign Bus = demultiplexer_1_out1 ? Instruction_Pointer[15:8] : 8'bz;  // Controlled_Buffer controlled_buffer_4
  Counter #(.width(16), .max('hffff)) IP (
    .load(or_1_out), .D(multiplexer_2_out), .count(IP_Advance), .Q(Instruction_Pointer), .clk(clock),
    .clr(Reset));  // open: carry
  RAM #(.addrWidth(16), .bus("separate")) ram_1 (
    .addr(multiplexer_1_out), .din(Bus), .data(Bus), .str(Memory_In), .clk(clock), .ld(Memory_out));  // open: sel, clr
  Register Low_2 (.D(Bus), .en(and_1_out), .Q(Stack_Pointer_Low), .clk(clock), .clr(Reset));
  Register High_2 (.D(Bus), .en(and_9_out), .Q(Stack_Pointer_High), .clk(clock), .clr(Reset));
  Register High_3 (.D(Bus), .en(and_10_out), .Q(Jump_Register_High), .clk(clock), .clr(Reset));
  Register Low_3 (.D(Bus), .en(and_4_out), .Q(Jump_Register_Low), .clk(clock), .clr(Reset));
  Register High_4 (.D(Bus), .en(and_11_out), .Q(RET_Register_High), .clk(clock), .clr(Reset));
  Register Low_4 (.D(Bus), .en(and_5_out), .Q(RET_Register_Low), .clk(clock), .clr(Reset));
  Pull_Resistor pull_resistor_1 (.node(Bus));
  assign Bus = demultiplexer_3_out0 ? Stack_Pointer_Low : 8'bz;  // Controlled_Buffer controlled_buffer_5
  assign Bus = demultiplexer_3_out1 ? Stack_Pointer_High : 8'bz;  // Controlled_Buffer controlled_buffer_6
  assign Bus = demultiplexer_4_out0 ? Jump_Register_Low : 8'bz;  // Controlled_Buffer controlled_buffer_7
  assign Bus = demultiplexer_4_out1 ? Jump_Register_High : 8'bz;  // Controlled_Buffer controlled_buffer_8
  assign Bus = demultiplexer_5_out0 ? RET_Register_Low : 8'bz;  // Controlled_Buffer controlled_buffer_9
  assign Bus = demultiplexer_5_out1 ? RET_Register_High : 8'bz;  // Controlled_Buffer controlled_buffer_10
  Register ALU1 (.D(Bus), .en(Alu_1_In), .Q(Register_ALU_1), .clk(clock), .clr(Reset));
  Register ALU2 (.D(Bus), .en(Alu_2_In), .Q(Register_ALU_2), .clk(clock), .clr(Reset));
  assign Bus = decoder_1_out0 ? Register_A : 8'bz;  // Controlled_Buffer controlled_buffer_11
  Register A (.D(Bus), .en(decoder_2_out0), .Q(Register_A), .clk(clock), .clr(Reset));
  Register B (.D(Bus), .en(decoder_2_out1), .Q(Register_B), .clk(clock), .clr(Reset));
  assign Bus = decoder_1_out1 ? Register_B : 8'bz;  // Controlled_Buffer controlled_buffer_12
  assign Bus = decoder_1_out2 ? Register_C : 8'bz;  // Controlled_Buffer controlled_buffer_13
  Register C (.D(Bus), .en(decoder_2_out2), .Q(Register_C), .clk(clock), .clr(Reset));
  Register D (.D(Bus), .en(decoder_2_out3), .Q(Register_D), .clk(clock), .clr(Reset));
  assign Bus = decoder_1_out3 ? Register_D : 8'bz;  // Controlled_Buffer controlled_buffer_14
  assign Bus = Alu_Out ? multiplexer_4_out : 8'bz;  // Controlled_Buffer controlled_buffer_15
  Adder adder_1 (.a(Register_ALU_1), .b(Register_ALU_2), .out(adder_1_out), .cin(Carry_In), .cout(Carry_out));
  Subtractor subtractor_1 (
    .a(Register_ALU_1), .b(Register_ALU_2), .out(subtractor_1_out), .bin(Carry_In), .bout(Alu2_GT_Alu1));
  assign nand_1_out = ~(Register_ALU_1 & Register_ALU_2);  // NAND_Gate nand_1, 8 bits wide
  assign xor_1_out = Register_ALU_1 ^ Register_ALU_2;  // XOR_Gate xor_1, 8 bits wide
  Decoder #(.select(2), .disabled(0)) decoder_1 (
    .out0(decoder_1_out0), .out1(decoder_1_out1), .out2(decoder_1_out2), .out3(decoder_1_out3),
    .sel({Register_Out_H, Register_Out_L}), .en(Register_Out_Enable));
  Decoder #(.select(2), .disabled(0)) decoder_2 (
    .out0(decoder_2_out0), .out1(decoder_2_out1), .out2(decoder_2_out2), .out3(decoder_2_out3),
    .sel({Register_In_H, Register_In_L}), .en(Register_In_Enable));
  nor nor_1 (nor_1_out, multiplexer_4_out[0], multiplexer_4_out[1], multiplexer_4_out[2], multiplexer_4_out[3], multiplexer_4_out[4], multiplexer_4_out[5], multiplexer_4_out[6], multiplexer_4_out[7]);
  Multiplexer #(.select(2), .width(8), .enable("false")) multiplexer_4 (
    .in0(adder_1_out), .in1(subtractor_1_out), .in2(nand_1_out), .in3(xor_1_out), .out(multiplexer_4_out),
    .sel({Alu_Op_H, Alu_Op_L}));
  Multiplexer #(.enable("false")) multiplexer_5 (.in0(nor_1_out), .in1(Reset), .out(Flag_zero), .sel(Reset));
  Multiplexer #(.enable("false")) multiplexer_6 (
    .in0(multiplexer_4_out[7]), .in1(Reset), .out(Flag_negative), .sel(Reset));
  ROM #(.addrWidth(16), .dataWidth(32)) rom_1 (
    .addr({Flag_negative, Alu2_GT_Alu1, Carry_out, Flag_zero, Micro_Counter, Instruction}),
    .data({SP_Select, SP_In, SP_Enable, FF_Out, One_Out, IP_Select, IP_Out, IP_Enable, rom_1_data[23:22], Alu_Out, Alu_Op_H, Alu_Op_L, Carry_In, Alu_2_In, Alu_1_In, Instruction_Register_Enable, Memory_out, IP_Advance, Memory_Input_Select, Write_Memory_Select, Write_Memory_Enable, Memory_In, Halt, Register_In_H, Register_In_L, Register_In_Enable, Register_Out_H, Register_Out_L, Register_Out_Enable, Micro_Reset, rom_1_data[0]}));  // open: sel
  ROM #(.addrWidth(16), .dataWidth(32)) rom_2 (
    .addr({Flag_negative, Alu2_GT_Alu1, Carry_out, Flag_zero, Micro_Counter, Instruction}),
    .data({rom_2_data, RET_Select, RET_Enable, RET_In, JMP_Select, JMP_Enable, JMP_In}));  // open: sel
  or or_2 (Reset, Reset_Button, rom_1_data[0]);
  Button button_1 (.out(Reset_Button));
  // Probe on Register_A
  // Probe on Register_B
  // Probe on Register_C
  // Probe on Register_D
  // Probe on Register_ALU_1
  // Probe on Register_ALU_2
  // Probe on Stack_Pointer_Low
  // Probe on Stack_Pointer_High
  // Probe on Jump_Register_Low
  // Probe on Jump_Register_High
  // Probe on RET_Register_Low
  // Probe on RET_Register_High
  Button button_2 (.out(button_2_out));
  Clock clock_1 (.out(clock_1_out));
  not not_1 (not_1_out, Micro_Reset);
  // Probe on Bus
  // Probe on Instruction
  // Probe on Micro_Counter
  // Probe on {Flag_negative, Alu2_GT_Alu1, Carry_out, Flag_zero}
  // Probe on Memory_Register_Low
  // Probe on Memory_Register_High
  // Probe on Instruction_Pointer
  and and_12 (and_12_out, Halt, button_2_out);
  and and_13 (and_13_out, ~Halt, clock_1_out);  // AND_Gate
  Counter #(.width(4), .max('hf)) counter_1 (
    .load(Micro_Reset), .D(4'b0000), .count(not_1_out), .Q(Micro_Counter), .clk(clock), .clr(Reset));  // open: carry
  or or_3 (clock, and_12_out, and_13_out);

  // Other names for the same wires on the sheet: Flags[3:0] = {Flag_negative, Alu2_GT_Alu1, Carry_out, Flag_zero}

  // Notes on the sheet:
  //   contents of rom_1 (hex, n*v repeats v):
  //   256*c000 256*2000 24 2c 34 3c 64 6c 74 7c a4 ac b4 bc e4 ec f4 fc 5020 5060 50a0 50e0 1204 120c 1214
  //   121c 1404 140c 1414 141c 1c04 1c0c 1c14 1c1c 4020 4060 40a0 40e0 20 60 a0 e0 4*2 1200 1200 5000 5000
  //   16*2 4*10004 4*1000c 4*10014 4*1001c 4*10004 4*1000c 4*10014 4*1001c 4*10004 4*1000c 4*10014 4*1001c
  //   4*10004 4*1000c 4*10014 4*1001c 4*24000 8*8020000 4*10000 48*2 4000 1000000 3000000 1000000 4*2002
  //   40*2 60000004 6000000c 60000014 6000001c e0000004 e000000c e0000014 e000001c 20010400 20010000
  //   20000400 4*2 100 32*2 4*2000 28*2 20004 2000c 20014 2001c 20004 2000c 20014 2001c 20004 2000c 20014
  //   2001c 20004 2000c 20014 2001c 20004 2000c 20014 2001c 20004 2000c 20014 2001c 20004 2000c 20014
  //   2001c 20004 2000c 20014 2001c 20004 2000c 20014 2001c 20004 2000c 20014 2001c 20004 2000c 20014
  //   2001c 20004 2000c 20014 2001c 20004 2000c 20014 2001c 20004 2000c 20014 2001c 20004 2000c 20014
  //   2001c 20004 2000c 20014 2001c 12004 1200c 12014 1201c 10004 1000c 10014 1001c 10004 1000c 10014
  //   1001c 20004 2000c 20014 2001c 48*2 2000 5000000 7000000 5000000 4*24000 48*2 8020000 8020000
  //   a0000c00 69*2 4*200020 4*200060 4*2000a0 4*2000e0 4*280020 4*280060 4*2800a0 4*2800e0 4*300020
  //   4*300060 4*3000a0 4*3000e0 4*380020 4*380060 4*3800a0 4*3800e0 200020 200060 2000a0 2000e0 200020
  //   200060 2000a0 2000e0 280020 280060 2800a0 2800e0 2c0020 2c0060 2c00a0 2c00e0 48*2 4000 2 1000000 2
  //   4*1240000 48*2 60280000 60200400 198*2 2000 2 5000000 53*2 20000 20000 202*2 4*7010000 48*2 a0010c00
  //   a0010000 202*2 4*5200000 48*2 e0280000 e0200c00 2054*2 256*c000 256*2000 24 2c 34 3c 64 6c 74 7c a4
  //   ac b4 bc e4 ec f4 fc 5020 5060 50a0 50e0 1204 120c 1214 121c 1404 140c 1414 141c 1c04 1c0c 1c14 1c1c
  //   4020 4060 40a0 40e0 20 60 a0 e0 4*2 1200 1200 5000 5000 16*2 4*10004 4*1000c 4*10014 4*1001c 4*10004
  //   4*1000c 4*10014 4*1001c 4*10004 4*1000c 4*10014 4*1001c 4*10004 4*1000c 4*10014 4*1001c 4*24000
  //   8*8020000 4*10000 48*2 4000 1000000 3000000 1000000 2002 3010000 2002 2002 40*2 60000004 6000000c
  //   60000014 6000001c e0000004 e000000c e0000014 e000001c 20010400 20010000 20000400 4*2 100 32*2 4*2000
  //   28*2 20004 2000c 20014 2001c 20004 2000c 20014 2001c 20004 2000c 20014 2001c 20004 2000c 20014 2001c
  //   20004 2000c 20014 2001c 20004 2000c 20014 2001c 20004 2000c 20014 2001c 20004 2000c 20014 2001c
  //   20004 2000c 20014 2001c 20004 2000c 20014 2001c 20004 2000c 20014 2001c 20004 2000c 20014 2001c
  //   20004 2000c 20014 2001c 20004 2000c 20014 2001c 20004 2000c 20014 2001c 20004 2000c 20014 2001c
  //   12004 1200c 12014 1201c 10004 1000c 10014 1001c 10004 1000c 10014 1001c 20004 2000c 20014 2001c 48*2
  //   2000 5000000 7000000 5000000 4*24000 48*2 8020000 8020000 a0000c00 69*2 4*200020 4*200060 4*2000a0
  //   4*2000e0 4*280020 4*280060 4*2800a0 4*2800e0 4*300020 4*300060 4*3000a0 4*3000e0 4*380020 4*380060
  //   4*3800a0 4*3800e0 200020 200060 2000a0 2000e0 200020 200060 2000a0 2000e0 280020 280060 2800a0
  //   2800e0 2c0020 2c0060 2c00a0 2c00e0 48*2 4000 2 1000000 2 4*1240000 48*2 60280000 60200400 198*2 2000
  //   2 5000000 53*2 20000 20000 202*2 4*7010000 48*2 a0010c00 a0010000 202*2 4*5200000 48*2 e0280000
  //   e0200c00 2054*2 256*c000 256*2000 24 2c 34 3c 64 6c 74 7c a4 ac b4 bc e4 ec f4 fc 5020 5060 50a0
  //   50e0 1204 120c 1214 121c 1404 140c 1414 141c 1c04 1c0c 1c14 1c1c 4020 4060 40a0 40e0 20 60 a0 e0 4*2
  //   1200 1200 5000 5000 16*2 4*10004 4*1000c 4*10014 4*1001c 4*10004 4*1000c 4*10014 4*1001c 4*10004
  //   4*1000c 4*10014 4*1001c 4*10004 4*1000c 4*10014 4*1001c 4*24000 8*8020000 4*10000 48*2 4000 1000000
  //   3000000 1000000 3010000 2002 2002 2002 40*2 60000004 6000000c 60000014 6000001c e0000004 e000000c
  //   e0000014 e000001c 20010400 20010000 20000400 4*2 100 32*2 4*2000 28*2 20004 2000c 20014 2001c 20004
  //   2000c 20014 2001c 20004 2000c 20014 2001c 20004 2000c 20014 2001c 20004 2000c 20014 2001c 20004
  //   2000c 20014 2001c 20004 2000c 20014 2001c 20004 2000c 20014 2001c 20004 2000c 20014 2001c 20004
  //   2000c 20014 2001c 20004 2000c 20014 2001c 20004 2000c 20014 2001c 20004 2000c 20014 2001c 20004
  //   2000c 20014 2001c 20004 2000c 20014 2001c 20004 2000c 20014 2001c 12004 120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
  //   contents of rom_2 (hex, n*v repeats v):
  //   256*c000 256*2000 24 2c 34 3c 64 6c 74 7c a4 ac b4 bc e4 ec f4 fc 5020 5060 50a0 50e0 1204 120c 1214
  //   121c 1404 140c 1414 141c 1c04 1c0c 1c14 1c1c 4020 4060 40a0 40e0 20 60 a0 e0 24*2 4*10004 4*1000c
  //   4*10014 4*1001c 4*10004 4*1000c 4*10014 4*1001c 4*10004 4*1000c 4*10014 4*1001c 4*10004 4*1000c
  //   4*10014 4*1001c 4*24000 8*8020000 4*10000 48*2 5004000 2 2 2 4*2002 40*2 60000004 6000000c 60000014
  //   6000001c e0000004 e000000c e0000014 e000001c 20010400 20010000 20000400 4*2 100 32*2 4*2000 28*2
  //   20004 2000c 20014 2001c 20004 2000c 20014 2001c 20004 2000c 20014 2001c 20004 2000c 20014 2001c
  //   20004 2000c 20014 2001c 20004 2000c 20014 2001c 20004 2000c 20014 2001c 20004 2000c 20014 2001c
  //   20004 2000c 20014 2001c 20004 2000c 20014 2001c 20004 2000c 20014 2001c 20004 2000c 20014 2001c
  //   20004 2000c 20014 2001c 20004 2000c 20014 2001c 20004 2000c 20014 2001c 20004 2000c 20014 2001c
  //   12004 1200c 12014 1201c 10004 1000c 10014 1001c 10004 1000c 10014 1001c 20004 2000c 20014 2001c 48*2
  //   2000 2 2 2 4*24000 48*2 8020000 8020000 a0000c00 69*2 4*200020 4*200060 4*2000a0 4*2000e0 4*280020
  //   4*280060 4*2800a0 4*2800e0 4*300020 4*300060 4*3000a0 4*3000e0 4*380020 4*380060 4*3800a0 4*3800e0
  //   200020 200060 2000a0 2000e0 200020 200060 2000a0 2000e0 280020 280060 2800a0 2800e0 2c0020 2c0060
  //   2c00a0 2c00e0 48*2 1004000 2 2 2 4*1240000 48*2 60280000 60200400 254*2 20000 20000 202*2 4*7010000
  //   48*2 a0010c00 a0010000 202*2 4*5200000 48*2 e0280000 e0200c00 2054*2 256*c000 256*2000 24 2c 34 3c
  //   64 6c 74 7c a4 ac b4 bc e4 ec f4 fc 5020 5060 50a0 50e0 1204 120c 1214 121c 1404 140c 1414 141c 1c04
  //   1c0c 1c14 1c1c 4020 4060 40a0 40e0 20 60 a0 e0 24*2 4*10004 4*1000c 4*10014 4*1001c 4*10004 4*1000c
  //   4*10014 4*1001c 4*10004 4*1000c 4*10014 4*1001c 4*10004 4*1000c 4*10014 4*1001c 4*24000 8*8020000
  //   4*10000 48*2 5004000 2 2 2 2002 3010000 2002 2002 40*2 60000004 6000000c 60000014 6000001c e0000004
  //   e000000c e0000014 e000001c 20010400 20010000 20000400 4*2 100 32*2 4*2000 28*2 20004 2000c 20014
  //   2001c 20004 2000c 20014 2001c 20004 2000c 20014 2001c 20004 2000c 20014 2001c 20004 2000c 20014
  //   2001c 20004 2000c 20014 2001c 20004 2000c 20014 2001c 20004 2000c 20014 2001c 20004 2000c 20014
  //   2001c 20004 2000c 20014 2001c 20004 2000c 20014 2001c 20004 2000c 20014 2001c 20004 2000c 20014
  //   2001c 20004 2000c 20014 2001c 20004 2000c 20014 2001c 20004 2000c 20014 2001c 12004 1200c 12014
  //   1201c 10004 1000c 10014 1001c 10004 1000c 10014 1001c 20004 2000c 20014 2001c 48*2 2000 2 2 2
  //   4*24000 48*2 8020000 8020000 a0000c00 69*2 4*200020 4*200060 4*2000a0 4*2000e0 4*280020 4*280060
  //   4*2800a0 4*2800e0 4*300020 4*300060 4*3000a0 4*3000e0 4*380020 4*380060 4*3800a0 4*3800e0 200020
  //   200060 2000a0 2000e0 200020 200060 2000a0 2000e0 280020 280060 2800a0 2800e0 2c0020 2c0060 2c00a0
  //   2c00e0 48*2 1004000 2 2 2 4*1240000 48*2 60280000 60200400 254*2 20000 20000 202*2 4*7010000 48*2
  //   a0010c00 a0010000 202*2 4*5200000 48*2 e0280000 e0200c00 2054*2 256*c000 256*2000 24 2c 34 3c 64 6c
  //   74 7c a4 ac b4 bc e4 ec f4 fc 5020 5060 50a0 50e0 1204 120c 1214 121c 1404 140c 1414 141c 1c04 1c0c
  //   1c14 1c1c 4020 4060 40a0 40e0 20 60 a0 e0 24*2 4*10004 4*1000c 4*10014 4*1001c 4*10004 4*1000c
  //   4*10014 4*1001c 4*10004 4*1000c 4*10014 4*1001c 4*10004 4*1000c 4*10014 4*1001c 4*24000 8*8020000
  //   4*10000 48*2 5004000 2 2 2 3010000 2002 2002 2002 40*2 60000004 6000000c 60000014 6000001c e0000004
  //   e000000c e0000014 e000001c 20010400 20010000 20000400 4*2 100 32*2 4*2000 28*2 20004 2000c 20014
  //   2001c 20004 2000c 20014 2001c 20004 2000c 20014 2001c 20004 2000c 20014 2001c 20004 2000c 20014
  //   2001c 20004 2000c 20014 2001c 20004 2000c 20014 2001c 20004 2000c 20014 2001c 20004 2000c 20014
  //   2001c 20004 2000c 20014 2001c 20004 2000c 20014 2001c 20004 2000c 20014 2001c 20004 2000c 20014
  //   2001c 20004 2000c 20014 2001c 20004 2000c 20014 2001c 20004 2000c 20014 2001c 12004 1200c 12014
  //   1201c 10004 1000c 10014 1001c 10004 1000c 10014 1001c 20004 2000c 20014 2001c 48*2 2000 2 2 2
  //   4*24000 48*2 8020000 8020000 a0000c00 69*2 4*200020 4*200060 4*2000a0 4*2000e0 4*280020 4*280060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
endmodule
