// Logisim project schema1.circ as structural Verilog: 1 circuit, main circuit main
module main (
  input  in_1,
  input  in_2,
  input  in_3,
  input  in_4
);

  wire Alu2_GT_Alu1, Alu_1_In, Alu_2_In, Alu_Op_H, Alu_Op_L, Alu_Out, and_1_out, and_2_out, button_1_out,
       button_2_out, Carry_In, Carry_out, clock, clock_1_out, decoder_1_out0, decoder_1_out1, decoder_1_out2,
       decoder_1_out3, decoder_2_out0, decoder_2_out1, decoder_2_out2, decoder_2_out3, demultiplexer_1_out0,
       demultiplexer_1_out1, FF_Out, Flag_negative, Flag_zero, Halt, Instruction_Register_Enable, IP_Advance,
       IP_Out_H, IP_Out_L, IP_Set_H, IP_Set_L, Memory_In, Memory_Input_Select, Memory_out, Micro_Reset,
       nor_1_out, not_1_out, One_Out, or_1_out, Register_In_Enable, Register_In_H, Register_In_L,
       Register_Out_Enable, Register_Out_H, Register_Out_L, Reset, Write_Memory_Enable, Write_Memory_Select,
       Zero_Out;
  wire [3:0] Micro_Counter;
  wire [7:0] A_q, adder_1_out, ALU1_q, ALU2_q, B_q, C_q, controlled_buffer_1_out, D_q, Instruction, IP_q,
       IP_q_2, multiplexer_4_out, nand_1_out, subtractor_1_out, xor_1_out;
  wire [15:0] Low_q, multiplexer_1_out, multiplexer_2_out;
  wire [31:0] rom_1_data;

  Button button_1 (.out(button_1_out));
  Clock clock_1 (.out(clock_1_out));
  not not_1 (not_1_out, Micro_Reset);
  or or_1 (or_1_out, IP_Set_L, IP_Set_H);
  Demultiplexer #(.enable("false")) demultiplexer_1 (
    .out0(demultiplexer_1_out0), .out1(demultiplexer_1_out1), .in(Write_Memory_Enable),
    .sel(Write_Memory_Select));
  Register High (.D(controlled_buffer_1_out), .en(demultiplexer_1_out1), .Q(Low_q[15:8]), .clk(clock), .clr(Reset));
  Multiplexer #(.width(16), .enable("false")) multiplexer_1 (
    .in0({IP_q_2, IP_q}), .in1(Low_q), .out(multiplexer_1_out), .sel(Memory_Input_Select));
  and and_1 (and_1_out, Halt, button_1_out);
  and and_2 (and_2_out, ~Halt, clock_1_out);  // AND_Gate
  Counter #(.width(4), .max('hf)) counter_1 (
    .load(Micro_Reset), .D(4'b0000), .count(not_1_out), .Q(Micro_Counter), .clk(clock), .clr(Reset));  // open: carry
  Multiplexer #(.width(8), .enable("false")) multiplexer_2 (
    .in0(IP_q), .in1(controlled_buffer_1_out), .out(multiplexer_2_out[7:0]), .sel(IP_Set_L));
  Multiplexer #(.width(8), .enable("false")) multiplexer_3 (
    .in0(IP_q_2), .in1(controlled_buffer_1_out), .out(multiplexer_2_out[15:8]), .sel(IP_Set_H));
  Register Low (.D(controlled_buffer_1_out), .en(demultiplexer_1_out0), .Q(Low_q[7:0]), .clk(clock), .clr(Reset));
  or or_2 (clock, and_1_out, and_2_out);
  assign controlled_buffer_1_out = IP_Out_L ? IP_q : 8'bz;  // Controlled_Buffer controlled_buffer_1
  assign controlled_buffer_1_out = IP_Out_H ? IP_q_2 : 8'bz;  // Controlled_Buffer controlled_buffer_2
  Counter #(.width(16), .max('hffff)) IP (
    .load(or_1_out), .D(multiplexer_2_out), .count(IP_Advance), .Q({IP_q_2, IP_q}), .clk(clock), .clr(Reset));  // open: carry
  RAM #(.addrWidth(16), .bus("separate")) ram_1 (
    .addr(multiplexer_1_out), .din(controlled_buffer_1_out), .data(controlled_buffer_1_out), .str(Memory_In),
    .clk(clock), .ld(Memory_out));  // open: sel, clr
  assign controlled_buffer_1_out = Zero_Out ? {8{1'b0}} : 8'bz;  // Controlled_Buffer controlled_buffer_3
  assign controlled_buffer_1_out = One_Out ? 8'h1 : 8'bz;  // Controlled_Buffer controlled_buffer_4
  assign controlled_buffer_1_out = FF_Out ? {8{1'b1}} : 8'bz;  // Controlled_Buffer controlled_buffer_5
  // Probe on controlled_buffer_1_out
  Register ALU1 (.D(controlled_buffer_1_out), .en(Alu_1_In), .Q(ALU1_q), .clk(clock), .clr(Reset));
  Register ALU2 (.D(controlled_buffer_1_out), .en(Alu_2_In), .Q(ALU2_q), .clk(clock), .clr(Reset));
  Register A (.D(controlled_buffer_1_out), .en(decoder_2_out0), .Q(A_q), .clk(clock), .clr(Reset));
  assign controlled_buffer_1_out = decoder_1_out0 ? A_q : 8'bz;  // Controlled_Buffer controlled_buffer_6
  Register B (.D(controlled_buffer_1_out), .en(decoder_2_out1), .Q(B_q), .clk(clock), .clr(Reset));
  assign controlled_buffer_1_out = decoder_1_out1 ? B_q : 8'bz;  // Controlled_Buffer controlled_buffer_7
  assign controlled_buffer_1_out = decoder_1_out2 ? C_q : 8'bz;  // Controlled_Buffer controlled_buffer_8
  Register C (.D(controlled_buffer_1_out), .en(decoder_2_out2), .Q(C_q), .clk(clock), .clr(Reset));
  Register D (.D(controlled_buffer_1_out), .en(decoder_2_out3), .Q(D_q), .clk(clock), .clr(Reset));
  assign controlled_buffer_1_out = decoder_1_out3 ? D_q : 8'bz;  // Controlled_Buffer controlled_buffer_9
  assign controlled_buffer_1_out = Alu_Out ? multiplexer_4_out : 8'bz;  // Controlled_Buffer controlled_buffer_10
  Adder adder_1 (.a(ALU1_q), .b(ALU2_q), .out(adder_1_out), .cin(Carry_In), .cout(Carry_out));
  Subtractor subtractor_1 (.a(ALU1_q), .b(ALU2_q), .out(subtractor_1_out), .bin(Carry_In), .bout(Alu2_GT_Alu1));
  assign nand_1_out = ~(ALU1_q & ALU2_q);  // NAND_Gate nand_1, 8 bits wide
  assign xor_1_out = ALU1_q ^ ALU2_q;  // XOR_Gate xor_1, 8 bits wide
  Decoder #(.select(2), .disabled(0)) decoder_1 (
    .out0(decoder_1_out0), .out1(decoder_1_out1), .out2(decoder_1_out2), .out3(decoder_1_out3),
    .sel({Register_Out_H, Register_Out_L}), .en(Register_Out_Enable));
  Decoder #(.select(2), .disabled(0)) decoder_2 (
    .out0(decoder_2_out0), .out1(decoder_2_out1), .out2(decoder_2_out2), .out3(decoder_2_out3),
    .sel({Register_In_H, Register_In_L}), .en(Register_In_Enable));
  Register register_1 (
    .D(controlled_buffer_1_out), .en(Instruction_Register_Enable), .Q(Instruction), .clk(clock), .clr(Reset));
  nor nor_1 (nor_1_out, multiplexer_4_out[0], multiplexer_4_out[1], multiplexer_4_out[2], multiplexer_4_out[3], multiplexer_4_out[4], multiplexer_4_out[5], multiplexer_4_out[6], multiplexer_4_out[7]);
  Multiplexer #(.select(2), .width(8), .enable("false")) multiplexer_4 (
    .in0(adder_1_out), .in1(subtractor_1_out), .in2(nand_1_out), .in3(xor_1_out), .out(multiplexer_4_out),
    .sel({Alu_Op_H, Alu_Op_L}));
  Multiplexer #(.enable("false")) multiplexer_5 (.in0(nor_1_out), .in1(Reset), .out(Flag_zero), .sel(Reset));
  Multiplexer #(.enable("false")) multiplexer_6 (
    .in0(multiplexer_4_out[7]), .in1(Reset), .out(Flag_negative), .sel(Reset));
  Button button_2 (.out(button_2_out));
  or or_3 (Reset, button_2_out, rom_1_data[0]);
  ROM #(.addrWidth(16), .dataWidth(32)) rom_1 (
    .addr({Flag_negative, Alu2_GT_Alu1, Carry_out, Flag_zero, Micro_Counter, Instruction}),
    .data({rom_1_data[31:29], FF_Out, One_Out, IP_Out_H, IP_Out_L, IP_Set_H, IP_Set_L, Zero_Out, Alu_Out, Alu_Op_H, Alu_Op_L, Carry_In, Alu_2_In, Alu_1_In, Instruction_Register_Enable, Memory_out, IP_Advance, Memory_Input_Select, Write_Memory_Select, Write_Memory_Enable, Memory_In, Halt, Register_In_H, Register_In_L, Register_In_Enable, Register_Out_H, Register_Out_L, Register_Out_Enable, Micro_Reset, rom_1_data[0]}));  // open: sel

  // Notes on the sheet:
  //   contents of rom_1 (hex, n*v repeats v):
  //   256*c000 256*2000 24 2c 34 3c 64 6c 74 7c a4 ac b4 bc e4 ec f4 fc 5020 5060 50a0 50e0 1204 120c 1214
  //   121c 1404 140c 1414 141c 1c04 1c0c 1c14 1c1c 4020 4060 40a0 40e0 400020 400060 4000a0 4000e0 24*2
  //   4*10004 4*1000c 4*10014 4*1001c 4*10004 4*1000c 4*10014 4*1001c 4*10004 4*1000c 4*10014 4*1001c
  //   4*10004 4*1000c 4*10014 4*1001c 4*24000 8*420000 4*410000 48*2 1004000 2 2 2 4*2002 55*2 100 32*2
  //   4*2000 28*2 20004 2000c 20014 2001c 20004 2000c 20014 2001c 20004 2000c 20014 2001c 20004 2000c
  //   20014 2001c 20004 2000c 20014 2001c 20004 2000c 20014 2001c 20004 2000c 20014 2001c 20004 2000c
  //   20014 2001c 20004 2000c 20014 2001c 20004 2000c 20014 2001c 20004 2000c 20014 2001c 20004 2000c
  //   20014 2001c 20004 2000c 20014 2001c 20004 2000c 20014 2001c 20004 2000c 20014 2001c 20004 2000c
  //   20014 2001c 12004 1200c 12014 1201c 10004 1000c 10014 1001c 10004 1000c 10014 1001c 20004 2000c
  //   20014 2001c 48*2 2000 2 2 2 4*24000 120*2 4*200020 4*200060 4*2000a0 4*2000e0 4*280020 4*280060
  //   4*2800a0 4*2800e0 4*300020 4*300060 4*3000a0 4*3000e0 4*380020 4*380060 4*3800a0 4*3800e0 200020
  //   200060 2000a0 2000e0 240020 240060 2400a0 2400e0 2c0020 2c0060 2c00a0 2c00e0 2c0020 2c0060 2c00a0
  //   2c00e0 48*2 804000 2 2 2 4*a40000 508*2 4*4010000 252*2 4*1200000 2104*2 256*c000 256*2000 24 2c 34
  //   3c 64 6c 74 7c a4 ac b4 bc e4 ec f4 fc 5020 5060 50a0 50e0 1204 120c 1214 121c 1404 140c 1414 141c
  //   1c04 1c0c 1c14 1c1c 4020 4060 40a0 40e0 400020 400060 4000a0 4000e0 24*2 4*10004 4*1000c 4*10014
  //   4*1001c 4*10004 4*1000c 4*10014 4*1001c 4*10004 4*1000c 4*10014 4*1001c 4*10004 4*1000c 4*10014
  //   4*1001c 4*24000 8*420000 4*410000 48*2 1004000 2 2 2 2002 2010000 2002 2002 55*2 100 32*2 4*2000
  //   28*2 20004 2000c 20014 2001c 20004 2000c 20014 2001c 20004 2000c 20014 2001c 20004 2000c 20014 2001c
  //   20004 2000c 20014 2001c 20004 2000c 20014 2001c 20004 2000c 20014 2001c 20004 2000c 20014 2001c
  //   20004 2000c 20014 2001c 20004 2000c 20014 2001c 20004 2000c 20014 2001c 20004 2000c 20014 2001c
  //   20004 2000c 20014 2001c 20004 2000c 20014 2001c 20004 2000c 20014 2001c 20004 2000c 20014 2001c
  //   12004 1200c 12014 1201c 10004 1000c 10014 1001c 10004 1000c 10014 1001c 20004 2000c 20014 2001c 48*2
  //   2000 2 2 2 4*24000 120*2 4*200020 4*200060 4*2000a0 4*2000e0 4*280020 4*280060 4*2800a0 4*2800e0
  //   4*300020 4*300060 4*3000a0 4*3000e0 4*380020 4*380060 4*3800a0 4*3800e0 200020 200060 2000a0 2000e0
  //   240020 240060 2400a0 2400e0 2c0020 2c0060 2c00a0 2c00e0 2c0020 2c0060 2c00a0 2c00e0 48*2 804000 2 2
  //   2 4*a40000 508*2 4*4010000 252*2 4*1200000 2104*2 256*c000 256*2000 24 2c 34 3c 64 6c 74 7c a4 ac b4
  //   bc e4 ec f4 fc 5020 5060 50a0 50e0 1204 120c 1214 121c 1404 140c 1414 141c 1c04 1c0c 1c14 1c1c 4020
  //   4060 40a0 40e0 400020 400060 4000a0 4000e0 24*2 4*10004 4*1000c 4*10014 4*1001c 4*10004 4*1000c
  //   4*10014 4*1001c 4*10004 4*1000c 4*10014 4*1001c 4*10004 4*1000c 4*10014 4*1001c 4*24000 8*420000
  //   4*410000 48*2 1004000 2 2 2 2010000 2002 2002 2002 55*2 100 32*2 4*2000 28*2 20004 2000c 20014 2001c
  //   20004 2000c 20014 2001c 20004 2000c 20014 2001c 20004 2000c 20014 2001c 20004 2000c 20014 2001c
  //   20004 2000c 20014 2001c 20004 2000c 20014 2001c 20004 2000c 20014 2001c 20004 2000c 20014 2001c
  //   20004 2000c 20014 2001c 20004 2000c 20014 2001c 20004 2000c 20014 2001c 20004 2000c 20014 2001c
  //   20004 2000c 20014 2001c 20004 2000c 20014 2001c 20004 2000c 20014 2001c 12004 1200c 12014 1201c
  //   10004 1000c 10014 1001c 10004 1000c 10014 1001c 20004 2000c 20014 2001c 48*2 2000 2 2 2 4*24000
  //   120*2 4*200020 4*200060 4*2000a0 4*2000e0 4*280020 4*280060 4*2800a0 4*2800e0 4*300020 4*300060
  //   4*3000a0 4*3000e0 4*380020 4*380060 4*3800a0 4*3800e0 200020 200060 2000a0 2000e0 240020 240060
  //   2400a0 2400e0 2c0020 2c0060 2c00a0 2c00e0 2c0020 2c0060 2c00a0 2c00e0 48*2 804000 2 2 2 4*a40000
  //   252*2 4*8020000 252*2 4*4010000 252*2 4*1200000 2104*2 256*c000 256*2000 24 2c 34 3c 64 6c 74 7c a4
  //   ac b4 bc e4 ec f4 fc 5020 5060 50a0 50e0 1204 120c 1214 121c 1404 140c 1414 141c 1c04 1c0c 1c14 1c1c
  //   4020 4060 40a0 40e0 400020 400060 4000a0 4000e0 24*2 4*10004 4*1000c 4*10014 4*1001c 4*10004 4*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
endmodule
